// Digital circuit accum.dig as structural Verilog
module accum (
  input  A3,
  input  B3,
  input  A2,
  input  B2,
  input  A1,
  input  B2_2,
  input  A0,
  input  B0,
  input  in_9,
  input  A7,
  input  B7,
  input  A6,
  input  B6,
  input  A5,
  input  B6_2,
  input  A4,
  input  B4,
  input  in_18,
  input  B8,
  input  B9,
  input  B13,
  input  B12,
  input  B12_2,
  input  B10,
  input  ADD_SUB,
  input  clk
);

  wire add_1_s, add_2_c_o, add_2_s, add_3_c_o, add_3_s, add_4_c_o, add_4_s, add_5_s, add_6_c_o, add_6_s,
       add_7_c_o, add_7_s, add_8_c_o, add_8_s, add_9_s, add_10_c_o, add_10_s, add_11_c_o, add_11_s,
       add_12_c_o, add_12_s, d_ff_1_q, d_ff_2_q, d_ff_3_q, d_ff_4_q, not_1_out, not_2_out, not_3_out,
       not_4_out, xor_1_out, xor_2_out, xor_3_out, xor_4_out, xor_5_out;

  Add add_1 (.a(A3), .b(B3), .c_i(add_2_c_o), .s(add_1_s));  // open: c_o
  Add add_2 (.a(A2), .b(B2), .c_i(add_3_c_o), .s(add_2_s), .c_o(add_2_c_o));
  Add add_3 (.a(A1), .b(B2_2), .c_i(add_4_c_o), .s(add_3_s), .c_o(add_3_c_o));
  Add add_4 (.a(A0), .b(B0), .c_i(in_9), .s(add_4_s), .c_o(add_4_c_o));
  LED led_1 (.in(add_1_s));
  LED led_2 (.in(add_2_s));
  LED led_3 (.in(add_3_s));
  LED led_4 (.in(add_4_s));
  not not_1 (not_1_out, B7);
  not not_2 (not_2_out, B6);
  not not_3 (not_3_out, B6_2);
  not not_4 (not_4_out, B4);
  Add add_5 (.a(A7), .b(not_1_out), .c_i(add_6_c_o), .s(add_5_s));  // open: c_o
  Add add_6 (.a(A6), .b(not_2_out), .c_i(add_7_c_o), .s(add_6_s), .c_o(add_6_c_o));
  Add add_7 (.a(A5), .b(not_3_out), .c_i(add_8_c_o), .s(add_7_s), .c_o(add_7_c_o));
  Add add_8 (.a(A4), .b(not_4_out), .c_i(in_18), .s(add_8_s), .c_o(add_8_c_o));
  LED led_5 (.in(add_5_s));
  LED led_6 (.in(add_6_s));
  LED led_7 (.in(add_7_s));
  LED led_8 (.in(add_8_s));
  xor xor_1 (xor_1_out, B8, B9);
  LED led_9 (.in(xor_1_out));
  xor xor_2 (xor_2_out, B13, ADD_SUB);
  xor xor_3 (xor_3_out, B12, ADD_SUB);
  xor xor_4 (xor_4_out, B12_2, ADD_SUB);
  xor xor_5 (xor_5_out, B10, ADD_SUB);
  Add add_9 (.a(d_ff_1_q), .b(xor_2_out), .c_i(add_10_c_o), .s(add_9_s));  // open: c_o
  Add add_10 (.a(d_ff_2_q), .b(xor_3_out), .c_i(add_11_c_o), .s(add_10_s), .c_o(add_10_c_o));
  Add add_11 (.a(d_ff_3_q), .b(xor_4_out), .c_i(add_12_c_o), .s(add_11_s), .c_o(add_11_c_o));
  Add add_12 (.a(d_ff_4_q), .b(xor_5_out), .c_i(ADD_SUB), .s(add_12_s), .c_o(add_12_c_o));
  D_FF d_ff_1 (.D(add_9_s), .C(clk), .Q(d_ff_1_q));  // open: nQ
  D_FF d_ff_2 (.D(add_10_s), .C(clk), .Q(d_ff_2_q));  // open: nQ
  D_FF d_ff_3 (.D(add_11_s), .C(clk), .Q(d_ff_3_q));  // open: nQ
  D_FF d_ff_4 (.D(add_12_s), .C(clk), .Q(d_ff_4_q));  // open: nQ
  LED led_10 (.in(d_ff_1_q));
  LED led_11 (.in(d_ff_2_q));
  LED led_12 (.in(d_ff_3_q));
  LED led_13 (.in(d_ff_4_q));
endmodule
